# Fritzing sketch progetto2_ledpushb (saved by Fritzing 0.9.2b)
breadboards: 1

parts:
  LED1 = LED - 5mm [color="Red (633nm)" package="5 mm [THT]"]
  R1 = Resistor [tolerance=±5% resistance=220 package=THT]
  S1 = Pushbutton [package="[THT]"]
  Componente1 = Arduino Uno (Rev3)
  R2 = Resistor [tolerance=±5% resistance=220 package=THT]

nets:
  N1: LED1.cathode, R1.Pin_1
  N2: LED1.anode, Componente1.GND, R2.Pin_1
  N3: R1.Pin_0, Componente1.D13/SCK
  N4: S1.Pin_1, S1.Pin_2, Componente1.D8, R2.Pin_0
  N5: S1.Pin_3, S1.Pin_4, Componente1.5V
